# Fritzing sketch circuit_design (saved by Fritzing 0.9.3b)
breadboards: 1

parts:
  Raspberry_Pi_1 = Raspberry Pi 3 [part_number=RPI-3-V1.2]
  S1 = Pushbutton [package="[THT]"]
  S2 = Pushbutton [package="[THT]"]
  S3 = Pushbutton [package="[THT]"]
  S4 = Pushbutton [package="[THT]"]
  LED4 = LED - 5mm [color="Yellow (595nm)" package="5 mm [THT]"]
  LED8 = LED - 5mm [color="Red (660nm)" package="5 mm [THT]"]
  LED9 = LED - 5mm [color="Red (660nm)" package="5 mm [THT]"]
  LED10 = LED - 5mm [color="Yellow (595nm)" package="5 mm [THT]"]
  LED11 = LED - 5mm [color="Red (660nm)" package="5 mm [THT]"]
  LED12 = LED - 5mm [color="Yellow (574nm)" package="5 mm [THT]"]
  LED13 = LED - 5mm [color="Red (660nm)" package="5 mm [THT]"]
  LED14 = LED - 5mm [color="Yellow (595nm)" package="5 mm [THT]"]
  R1 = Resistor [tolerance=±5% resistance=220 package=THT]
  R2 = Resistor [tolerance=±5% resistance=220 package=THT]
  R3 = Resistor [tolerance=±5% resistance=220 package=THT]
  R4 = Resistor [tolerance=±5% resistance=220 package=THT]

nets:
  N1: Raspberry_Pi_1.3v3, S1.Pin_3, S1.Pin_4, S2.Pin_3, S2.Pin_4, S3.Pin_3, S3.Pin_4, S4.Pin_3, S4.Pin_4
  N2: Raspberry_Pi_1.GPIO17, S1.Pin_1, S1.Pin_2, R1.Pin_0
  N3: Raspberry_Pi_1.GPIO27, S2.Pin_1, S2.Pin_2, R2.Pin_0
  N4: Raspberry_Pi_1.GPIO22, S3.Pin_1, S3.Pin_2, R3.Pin_0
  N5: Raspberry_Pi_1.GPIO10, S4.Pin_1, S4.Pin_2, R4.Pin_0
  N6: Raspberry_Pi_1.GND, LED4.anode, LED8.anode, LED9.anode, LED10.anode, LED11.anode, LED12.anode, LED13.anode, LED14.anode, R1.Pin_1, R2.Pin_1, R3.Pin_1, R4.Pin_1
  N7: Raspberry_Pi_1.GPIO7, LED8.cathode
  N8: Raspberry_Pi_1.GPIO8, LED4.cathode
  N9: Raspberry_Pi_1.GPIO25, LED9.cathode
  N10: Raspberry_Pi_1.GPIO24, LED10.cathode
  N11: Raspberry_Pi_1.GPIO23, LED11.cathode
  N12: Raspberry_Pi_1.GPIO18, LED12.cathode
  N13: Raspberry_Pi_1.GPIO15, LED13.cathode
  N14: Raspberry_Pi_1.GPIO14, LED14.cathode
